# Fritzing sketch CIRCUIT (saved by Fritzing 0.9.3b)
breadboards: 1

parts:
  Gizwits_WiFi_Witty_ESP-12F1 = Gizwits WiFi Witty ESP-12F
  Grove1 = Grove OLED 128x96
  S1 = Momentary Switch [package=ksa_sealed_tac_switch]
  S2 = Momentary Switch [package=ksa_sealed_tac_switch]
  LED1 = smd LED [color="Red (633nm)" package="0603 [SMD]"]
  LED2 = LED - 3mm [color="Red (633nm)" package="3 mm [THT]"]
  M1 = Humidity and Temperature Sensor DHT11
  R1 = Resistor [tolerance=±5% resistance=220 package="1206 [SMD]"]
  R2 = Resistor [tolerance=±5% resistance=220 package="1206 [SMD]"]

nets:
  N1: Gizwits_WiFi_Witty_ESP-12F1.GPIO16, S1.2
  N2: Gizwits_WiFi_Witty_ESP-12F1.GPIO12, M1.Data
  N3: Gizwits_WiFi_Witty_ESP-12F1.GPIO13, S2.2
  N4: Gizwits_WiFi_Witty_ESP-12F1.GPIO15, R2.Pin_0
  N5: Gizwits_WiFi_Witty_ESP-12F1.GPIO2, R1.Pin_0
  N6: Gizwits_WiFi_Witty_ESP-12F1.GPIO4, Grove1.SDA
  N7: Gizwits_WiFi_Witty_ESP-12F1.GPIO5, Grove1.SCL
  GND: Grove1.GND, S1.3, S2.3, LED1.cathode, LED2.cathode, M1.GND
  VCC: Grove1.VCC, M1.Vcc
  N8: LED1.anode, R1.Pin_1
  N9: LED2.anode, R2.Pin_1

custom parts:
  Humidity and Temperature Sensor DHT11: Digital relative humidity & temperature sensor DHT11
